# Fritzing sketch Fritzing sketch for InfraRed Sensor (saved by Fritzing 0.7.10b)
breadboards: 2

parts:
  Arduino1 = Arduino
  Q1 = PHOTOTRANSISTOR REFLECTIVE OBJECT SENSOR [package=qrb1114-side]  # not connected
  LED1 = LED - 5mm [color="Red (633nm)" package="5 mm [THT]"]
  R1 = Resistor [tolerance=±1% resistance=330 package=THT]  # not connected
  R2 = Resistor [tolerance=±1% resistance=330 package=THT]
  R3 = Resistor [tolerance=±1% resistance=10k package=THT]
  LED2 = LED - 5mm [color="Infrared (880nm)" package="5 mm [THT]"]
  LED3 = LEDs [color="Infrared (940nm)" package=led5mm]  # not connected
  LED4 = LED - 5mm [color="Infrared (940nm)" package="5 mm [THT]"]  # not connected

nets:
  N1: Arduino1.+5V, R2.Pin_1, R3.Pin_0
  N2: Arduino1.GND, LED1.anode, LED2.anode
  N3: Arduino1.A0, R3.Pin_1
  N4: R2.Pin_0, LED2.cathode

notes:
  Alert!! LED
  Glows when there is an obstruction between the Infra Red Tx and Rx pair.
  They must be at a distance not greater than 6 inches apart.
  Infra Red Transmitter LED
  IR Receiver (Photo Diode)
  10 KΩ
  330 Ω
